// Logisim project D8421_plus_1.circ as structural Verilog: 2 circuits, main circuit main
module main (
  input  [3:0] in_1,
  output [3:0] out_2
);

  wire and_1_out, and_2_out, and_3_out, and_4_out, and_5_out, and_6_out, and_7_out, and_8_out, and_9_out,
       not_1_out, not_2_out, not_3_out;

  // Probe on in_1
  not not_1 (not_1_out, in_1[3]);
  not not_2 (not_2_out, in_1[2]);
  not not_3 (not_3_out, in_1[1]);
  not not_4 (out_2[0], in_1[0]);
  and and_1 (and_1_out, in_1[3], not_3_out);
  and and_2 (and_2_out, in_1[3], out_2[0]);
  and and_3 (and_3_out, in_1[3], not_2_out);
  and and_4 (and_4_out, not_1_out, in_1[2], in_1[1], in_1[0]);
  and and_5 (and_5_out, in_1[2], not_3_out);
  and and_6 (and_6_out, in_1[2], out_2[0]);
  and and_7 (and_7_out, not_2_out, in_1[1], in_1[0]);
  and and_8 (and_8_out, not_3_out, in_1[0]);
  and and_9 (and_9_out, in_1[1], out_2[0]);
  or or_1 (out_2[3], and_1_out, and_2_out, and_3_out, and_4_out);
  or or_2 (out_2[2], and_5_out, and_6_out, and_7_out);
  or or_3 (out_2[1], and_8_out, and_8_out, and_9_out, and_9_out);
  // Probe on out_2

  // Notes on the sheet:
  //   A
  //   B
  //   !A
  //   C
  //   D
  //   !B
  //   !D
  //   !C
endmodule

module main_f (
  input  [7:0] in_1,
  input  [7:0] in_2,
  output [7:0] out_3
);

  wire main_1_p3, main_1_p4, main_2_p5, main_3_p5, main_4_p5, main_5_p5, main_6_p5, main_7_p5;

  // Probe on in_1
  // Probe on in_2
  // main main_1: pin names not known; wires that end beside it: in_1[0], in_2[0], main_1_p3, main_1_p4, out_3[0]
  // main main_2: pin names not known; wires that end beside it: main_1_p3, in_1[1], in_2[1], main_1_p4, main_2_p5, out_3[1]
  // main main_3: pin names not known; wires that end beside it: main_1_p4, in_1[2], in_2[2], main_2_p5, main_3_p5, out_3[2]
  // main main_4: pin names not known; wires that end beside it: main_2_p5, in_1[3], in_2[3], main_3_p5, main_4_p5, out_3[3]
  // main main_5: pin names not known; wires that end beside it: main_3_p5, in_1[4], in_2[4], main_4_p5, main_5_p5, out_3[4]
  // main main_6: pin names not known; wires that end beside it: main_4_p5, in_1[5], in_2[5], main_5_p5, main_6_p5, out_3[5]
  // main main_7: pin names not known; wires that end beside it: main_5_p5, in_1[6], in_2[6], main_6_p5, main_7_p5, out_3[6]
  // main main_8: pin names not known; wires that end beside it: main_6_p5, in_1[7], in_2[7], main_7_p5, main_1_p3, out_3[7]
  // Probe on out_3
endmodule
