// Logisim project trigger.circ as structural Verilog: 1 circuit, main circuit main
module main (
);

  wire and_1_out, and_2_out, clock_1_out, T1_qn, T2_qn, T3_qn;
  wire [3:0] T1_q;

  and and_1 (and_1_out, T1_qn, T2_qn, T3_qn);
  and and_2 (and_2_out, T1_qn, T2_qn);
  Clock clock_1 (.out(clock_1_out));
  T_Flip_Flop T4 (.clk(clock_1_out), .T(and_1_out), .Q(T1_q[3]));  // open: Qn, preset, reset, en
  T_Flip_Flop T3 (.clk(clock_1_out), .T(and_2_out), .Q(T1_q[2]), .Qn(T3_qn));  // open: preset, reset, en
  T_Flip_Flop T2 (.clk(clock_1_out), .T(T1_qn), .Q(T1_q[1]), .Qn(T2_qn));  // open: preset, reset, en
  T_Flip_Flop T1 (.clk(clock_1_out), .T(1'b1), .Q(T1_q[0]), .Qn(T1_qn));  // open: preset, reset, en
  // Probe on T1_q
endmodule
